# Fritzing sketch MotionSketch (saved by Fritzing 0.9.3b)
circuit board: 8.46667cm x 5.64444cm
breadboards: 1

parts:
  nano = Arduino Nano (Rev3.0)
  power = Battery
  switch = Tilt Switch [package=THT]
  sonic = hc-sr04
  R1 = Resistor [tolerance=±5% resistance=220 package=THT]
  R2 = Resistor [tolerance=±5% resistance=220 package=THT]
  redLight = LED - 5mm [color="Red (633nm)" package="5 mm [THT]"]
  greenLight = LED - 5mm [color="Green (570nm)" package="5 mm [THT]"]
  speaker = Piezo Speaker

nets:
  N1: nano.D1/TX, nano.D7, R1.Pin_0, R2.Pin_0, speaker.pin1, speaker.pin2
  GND: nano.GND, power.-, switch.Pin_1, sonic.GND
  N2: nano.D8, redLight.cathode
  N3: nano.D9, greenLight.cathode
  N4: nano.D10, sonic.Trig
  N5: nano.D11/MOSI, sonic.Echo
  N6: nano.VIN, power.+, switch.Pin_2
  5V: nano.5V, sonic.VCC
  N7: R1.Pin_1, redLight.anode
  N8: R2.Pin_1, greenLight.anode
